// Logisim project Lab01_Mux21.circ as structural Verilog: 1 circuit, main circuit main
module main (
  input  Sel,
  input  ln1,
  input  ln2,
  output Out1
);

  wire and_1_out, and_2_out, not_1_out, not_2_out;

  not not_1 (not_1_out, Sel);
  not not_2 (not_2_out, not_1_out);
  and and_1 (and_1_out, not_2_out, ln1);
  and and_2 (and_2_out, not_1_out, ln2);
  or or_1 (Out1, and_1_out, and_2_out);

  // Notes on the sheet:
  //   Nuraly Zholaman 
  //   May 16, 2024
  //   Lab 01: 2-Way, 1-Bit multiplexer
endmodule
