// Logisim project Lab02_Bool.circ as structural Verilog: 3 circuits, main circuit main
module main (
  input  A1,
  input  B1,
  input  C1,
  input  A2,
  input  B2,
  input  C2,
  input  D2,
  output True1,
  output True2
);

  Equation_1 equation_1_1 (.In1A(A1), .In1B(B1), .In1C(C1), .Out1(True1));
  Equaion_2 Equation_2 (.ln2A(A2), .ln2B(B2), .ln2C(C2), .ln2D(D2), .Out2(True2));

  // Notes on the sheet:
  //   Nuraly Zholaman 
  //   May 16, 2024
  //   Lab 02: Boolean Equations
endmodule

module Equation_1 (
  input  In1A,
  input  In1B,
  input  In1C,
  output Out1
);

  wire and_1_out, and_2_out, and_3_out;

  and and_1 (and_1_out, ~In1A, In1B, ~In1C);  // AND_Gate
  and and_2 (and_2_out, In1A, ~In1B, ~In1C);  // AND_Gate
  and and_3 (and_3_out, In1A, In1B, In1C);
  or or_1 (Out1, and_1_out, and_2_out, and_3_out);
endmodule

module Equaion_2 (
  input  ln2A,
  input  ln2B,
  input  ln2C,
  input  ln2D,
  output Out2
);

  wire and_1_out, and_2_out, and_3_out, and_4_out;

  and and_1 (and_1_out, ~ln2A, ~ln2B, ln2C, ~ln2D);  // AND_Gate
  and and_2 (and_2_out, ~ln2A, ln2B, ln2C, ln2D);  // AND_Gate
  and and_3 (and_3_out, ln2A, ~ln2B, ln2C, ~ln2D);  // AND_Gate
  and and_4 (and_4_out, ln2A, ln2B, ln2C, ~ln2D);  // AND_Gate
  or or_1 (Out2, and_1_out, and_2_out, and_3_out, and_4_out);
endmodule
