// Logisim project Lab04_ALU.circ as structural Verilog: 4 circuits, main circuit main
module main (
  input  CIn,
  input  [3:0] InA,
  input  [3:0] InB,
  input  [2:0] Sel,
  input  Mode,
  output Cout,
  output Cmp,
  output [3:0] AluOut
);

  ALU alu_1 (.CIn(CIn), .InA(InA), .InB(InB), .Sel(Sel), .Mode(Mode), .COut(Cout), .Cmp(Cmp), .AluOut(AluOut));

  // Notes on the sheet:
  //   Nuraly Zholaman
  //   Lab04: ALU
  //   May 18, 2024
endmodule

module ALU (
  input  CIn,
  input  [3:0] InA,
  input  [3:0] InB,
  input  [2:0] Sel,
  input  Mode,
  output COut,
  output Cmp,
  output [3:0] AluOut
);

  wire [3:0] arithmetic_1_arout, logic_1_loout;

  Arithmetic arithmetic_1 (
    .CIn(CIn), .InA(InA), .InB(InB), .Sel(Sel), .ArOut(arithmetic_1_arout), .COut(COut), .Cmp(Cmp));
  Logic logic_1 (.InA(InA), .InB(InB), .Sel(Sel), .LoOut(logic_1_loout));
  Multiplexer #(.width(4)) multiplexer_1 (.in0(arithmetic_1_arout), .in1(logic_1_loout), .out(AluOut), .sel(Mode));

  // Notes on the sheet:
  //   Mode: H-Logic, L-Arithmetic
endmodule

module Arithmetic (
  input  CIn,
  input  [3:0] InA,
  input  [3:0] InB,
  input  [2:0] Sel,
  output [3:0] ArOut,
  output COut,
  output Cmp
);

  wire adder_1_cout, adder_2_cout, adder_3_cout, subtractor_1_bout, subtractor_2_bout, subtractor_3_bout,
       subtractor_4_bout;
  wire [3:0] adder_1_out, adder_2_out, adder_3_out, multiplier_1_out, multiplier_2_out, not_1_out, not_2_out,
       subtractor_1_out, subtractor_2_out, subtractor_3_out, subtractor_4_out;

  assign not_1_out = ~InB;  // NOT_Gate not_1, 4 bits wide
  Subtractor #(.width(4)) subtractor_1 (
    .a(InA), .b(4'b0001), .out(subtractor_1_out), .bin(CIn), .bout(subtractor_1_bout));
  Adder #(.width(4)) adder_1 (.a(InA), .b(InB), .out(adder_1_out), .cin(CIn), .cout(adder_1_cout));
  Subtractor #(.width(4)) subtractor_2 (.a(InA), .b(InB), .out(subtractor_2_out), .bin(CIn), .bout(subtractor_2_bout));
  Multiplier #(.width(4)) multiplier_1 (.a(InA), .b(InB), .out(multiplier_1_out));  // open: cin, cout
  Subtractor #(.width(4)) subtractor_3 (
    .a(multiplier_1_out), .b(4'b0001), .out(subtractor_3_out), .bout(subtractor_3_bout));  // open: bin
  Multiplier #(.width(4)) multiplier_2 (.a(InA), .b(not_1_out), .out(multiplier_2_out));  // open: cin, cout
  Subtractor #(.width(4)) subtractor_4 (
    .a(multiplier_2_out), .b(4'b0001), .out(subtractor_4_out), .bout(subtractor_4_bout));  // open: bin
  Adder #(.width(4)) adder_2 (.a(InA), .b(InA), .out(adder_2_out), .cin(CIn), .cout(adder_2_cout));
  Adder #(.width(4)) adder_3 (.a(InA), .b(4'b0001), .out(adder_3_out), .cin(CIn), .cout(adder_3_cout));
  Comparator #(.width(4)) comparator_1 (.a(InA), .b(InB), .eq(Cmp));  // open: gt, lt
  assign not_2_out = ~4'b0001;  // NOT_Gate not_2, 4 bits wide
  Multiplexer #(.select(3), .width(4)) multiplexer_1 (
    .in0(not_2_out), .in1(subtractor_1_out), .in2(adder_1_out), .in3(subtractor_2_out),
    .in4(subtractor_3_out), .in5(subtractor_4_out), .in6(adder_2_out), .in7(adder_3_out), .out(ArOut),
    .sel(Sel));
  Multiplexer #(.select(3)) multiplexer_2 (
    .in0(1'b0), .in1(subtractor_1_bout), .in2(adder_1_cout), .in3(subtractor_2_bout),
    .in4(subtractor_3_bout), .in5(subtractor_4_bout), .in6(adder_2_cout), .in7(adder_3_cout), .out(COut),
    .sel(Sel));

  // Notes on the sheet:
  //   Arithmetic Subcircuit
endmodule

module Logic (
  input  [3:0] InA,
  input  [3:0] InB,
  input  [2:0] Sel,
  output [3:0] LoOut
);

  wire [3:0] and_1_out, and_2_out, nand_1_out, nor_1_out, not_1_out, not_2_out, not_3_out, or_1_out,
       or_2_out, xor_1_out;

  assign not_1_out = ~InB;  // NOT_Gate not_1, 4 bits wide
  assign not_2_out = ~InB;  // NOT_Gate not_2, 4 bits wide
  assign not_3_out = ~InA;  // NOT_Gate not_3, 4 bits wide
  assign and_1_out = InA & InB;  // AND_Gate and_1, 4 bits wide
  assign nand_1_out = ~(InA & InB);  // NAND_Gate nand_1, 4 bits wide
  assign or_1_out = InA | InB;  // OR_Gate or_1, 4 bits wide
  assign nor_1_out = ~(InA | InB);  // NOR_Gate nor_1, 4 bits wide
  assign xor_1_out = InA ^ InB;  // XOR_Gate xor_1, 4 bits wide
  assign and_2_out = InA & not_1_out;  // AND_Gate and_2, 4 bits wide
  assign or_2_out = InA | not_2_out;  // OR_Gate or_2, 4 bits wide
  Multiplexer #(.select(3), .width(4)) multiplexer_1 (
    .in0(and_1_out), .in1(nand_1_out), .in2(or_1_out), .in3(nor_1_out), .in4(xor_1_out), .in5(and_2_out),
    .in6(or_2_out), .in7(not_3_out), .out(LoOut), .sel(Sel));

  // Notes on the sheet:
  //   Logic Subcircuit
endmodule
