// Logisim project Lab05_Counter.circ as structural Verilog: 7 circuits, main circuit main
module main (
  input  Rst,
  input  [2:0] Sel,
  output [3:0] Probe1
);

  wire Clk_out;

  Clock #(.highDuration(4), .lowDuration(4)) Clk (.out(Clk_out));
  Clock Sysclk ();  // open: out
  Universal universal_1 (.Clk(Clk_out), .Rst(Rst), .Sel(Sel), .OutUn(Probe1));
  Hex_Digit_Display hex_digit_display_1 (.value(Probe1));  // open: dp

  // Notes on the sheet:
  //   Nuraly Zholaman
  //   Lab05: Counters 
  //   May 18, 2024
endmodule

module up (
  input  Clk,
  input  Rst,
  output [3:0] OutUp
);

  wire d_ff_1_qn, d_ff_2_qn, d_ff_3_qn, d_ff_4_qn;

  D_Flip_Flop d_ff_1 (.D(d_ff_1_qn), .clk(Clk), .Q(OutUp[0]), .Qn(d_ff_1_qn), .reset(Rst));  // open: preset
  D_Flip_Flop d_ff_2 (.D(d_ff_2_qn), .clk(d_ff_1_qn), .Q(OutUp[1]), .Qn(d_ff_2_qn), .reset(Rst));  // open: preset
  D_Flip_Flop d_ff_3 (.D(d_ff_3_qn), .clk(d_ff_2_qn), .Q(OutUp[2]), .Qn(d_ff_3_qn), .reset(Rst));  // open: preset
  D_Flip_Flop d_ff_4 (.D(d_ff_4_qn), .clk(d_ff_3_qn), .Q(OutUp[3]), .Qn(d_ff_4_qn), .reset(Rst));  // open: preset
endmodule

module down (
  input  Clk,
  input  Rst,
  output [3:0] OutDown
);

  wire d_ff_1_qn, d_ff_2_qn, d_ff_3_qn, d_ff_4_qn;

  D_Flip_Flop d_ff_1 (.D(d_ff_1_qn), .clk(Clk), .Q(OutDown[0]), .Qn(d_ff_1_qn), .preset(Rst));  // open: reset
  D_Flip_Flop d_ff_2 (.D(d_ff_2_qn), .clk(OutDown[0]), .Q(OutDown[1]), .Qn(d_ff_2_qn), .preset(Rst));  // open: reset
  D_Flip_Flop d_ff_3 (.D(d_ff_3_qn), .clk(OutDown[1]), .Q(OutDown[2]), .Qn(d_ff_3_qn), .preset(Rst));  // open: reset
  D_Flip_Flop d_ff_4 (.D(d_ff_4_qn), .clk(OutDown[2]), .Q(OutDown[3]), .Qn(d_ff_4_qn), .preset(Rst));  // open: reset
endmodule

module Decade (
  input  Clk,
  input  Rst,
  output [3:0] OutDec
);

  wire and_1_out, d_ff_1_qn, d_ff_2_qn, d_ff_3_qn, d_ff_4_qn, or_1_out;

  D_Flip_Flop d_ff_1 (.D(d_ff_1_qn), .clk(Clk), .Q(OutDec[0]), .Qn(d_ff_1_qn), .reset(or_1_out));  // open: preset
  or or_1 (or_1_out, Rst, and_1_out);
  D_Flip_Flop d_ff_2 (.D(d_ff_2_qn), .clk(d_ff_1_qn), .Q(OutDec[1]), .Qn(d_ff_2_qn), .reset(or_1_out));  // open: preset
  D_Flip_Flop d_ff_3 (.D(d_ff_3_qn), .clk(d_ff_2_qn), .Q(OutDec[2]), .Qn(d_ff_3_qn), .reset(or_1_out));  // open: preset
  D_Flip_Flop d_ff_4 (.D(d_ff_4_qn), .clk(d_ff_3_qn), .Q(OutDec[3]), .Qn(d_ff_4_qn), .reset(or_1_out));  // open: preset
  and and_1 (and_1_out, OutDec[3], OutDec[1]);
endmodule

module ring (
  input  Clk,
  input  Rst,
  output [3:0] OutRing
);

  D_Flip_Flop d_ff_1 (.D(OutRing[3]), .clk(Clk), .Q(OutRing[0]), .preset(Rst));  // open: Qn, reset
  D_Flip_Flop d_ff_2 (.D(OutRing[0]), .clk(Clk), .Q(OutRing[1]), .reset(Rst));  // open: Qn, preset
  D_Flip_Flop d_ff_3 (.D(OutRing[1]), .clk(Clk), .Q(OutRing[2]), .reset(Rst));  // open: Qn, preset
  D_Flip_Flop d_ff_4 (.D(OutRing[2]), .clk(Clk), .Q(OutRing[3]), .reset(Rst));  // open: Qn, preset
endmodule

module johnson (
  input  Clk,
  input  Rst,
  output [3:0] OutJohn
);

  wire d_ff_4_qn;

  D_Flip_Flop d_ff_1 (.D(d_ff_4_qn), .clk(Clk), .Q(OutJohn[0]), .preset(Rst));  // open: Qn, reset
  D_Flip_Flop d_ff_2 (.D(OutJohn[0]), .clk(Clk), .Q(OutJohn[1]), .reset(Rst));  // open: Qn, preset
  D_Flip_Flop d_ff_3 (.D(OutJohn[1]), .clk(Clk), .Q(OutJohn[2]), .reset(Rst));  // open: Qn, preset
  D_Flip_Flop d_ff_4 (.D(OutJohn[2]), .clk(Clk), .Q(OutJohn[3]), .Qn(d_ff_4_qn), .reset(Rst));  // open: preset
endmodule

module Universal (
  input  Clk,
  input  Rst,
  input  [2:0] Sel,
  output [3:0] OutUn
);

  wire [3:0] decade_1_outdec, down_1_outdown, johnson_1_outjohn, ring_1_outring, up_1_outup;

  up up_1 (.Clk(Clk), .Rst(Rst), .OutUp(up_1_outup));
  down down_1 (.Clk(Clk), .Rst(Rst), .OutDown(down_1_outdown));
  Decade decade_1 (.Clk(Clk), .Rst(Rst), .OutDec(decade_1_outdec));
  ring ring_1 (.Clk(Clk), .Rst(Rst), .OutRing(ring_1_outring));
  johnson johnson_1 (.Clk(Clk), .Rst(Rst), .OutJohn(johnson_1_outjohn));
  Multiplexer #(.select(3), .width(4)) multiplexer_1 (
    .in0(up_1_outup), .in1(down_1_outdown), .in2(decade_1_outdec), .in3(ring_1_outring),
    .in4(johnson_1_outjohn), .out(OutUn), .sel(Sel));  // open: in5, in6, in7
endmodule
